// Digital circuit CPU.dig as structural Verilog
module CPU (
  input  RST,
  input  CLK,
  input  clk_2,
  input  CLK_SEL,
  input  EXTERNAL_BUTTON,
  output [7:0] opcode,
  output [15:0] rom
);

  wire A_LD, A_OE, A_SEL, addr_dec_1_nram_cs, addr_dec_1_nrom_cs, alu_1_c_flag, alu_1_n_flag, alu_1_v_flag,
       alu_1_z_flag, ALU_CIN, ALU_S0, ALU_S1, ALU_S2, and_1_out, and_2_out, B_SET, C, CLK_t, FL_SEL, I,
       I_SET, I_WRITE, irq_latch_1_p5, MAR_DIR, MEM_RD, MEM_WR, N, nALU_OE, nCLR_IRQ, nFL_LD, nFL_OE,
       nHBA_OE, nIR_LD, nIRA_OE, nIRD_OE, nMAR_INC, nMAR_OE, nMARH_LD, nMARL_LD, nMMIO_CS, nMPC_RST,
       not_2_out, nPC_LD, nPCH_OE, nPCL_OE, nRST, nSHR, nSP_INC, nSP_LD, nSP_OE, nSPH_OE, nSPL_OE, nV_OE,
       nXY_AOE, nXY_INC, PC_INC, PC_OE, REG_LD, REG_OE, Rsrc, SHR_IN0, SP_DIR, V, V_B0, XY_DIR, Z;
  wire [2:0] micropc_1_microstep;
  wire [7:0] alu_1_alu, int_vect_1_p3, int_vect_1_p3_2, mmio_1_spi_out, pc_1_d_out;
  wire [15:13] ctrlunit_1_c32_47;

  not not_1 (nRST, RST);
  and and_1 (and_1_out, CLK, ~CLK_SEL);  // And
  and and_2 (and_2_out, CLK_SEL, clk_2);
  or or_1 (CLK_t, and_1_out, and_2_out);
  // INT_VECT int_vect_1: pin names not known; wires that end beside it: nV_OE, V_B0, {int_vect_1_p3, int_vect_1_p3_2}
  not not_2 (not_2_out, RST);
  // A_H__BUFFER a_h__buffer_1: pin names not known; wires that end beside it: nHBA_OE
  // RST_Buffer rst_buffer_1: pin names not known; wires that end beside it: not_2_out, int_vect_1_p3, {int_vect_1_p3, int_vect_1_p3_2}
  ADDR_DEC addr_dec_1 (
    .A_IN({int_vect_1_p3, int_vect_1_p3_2}), .nRAM_CS(addr_dec_1_nram_cs), .nROM_CS(addr_dec_1_nrom_cs),
    .nMMIO_CS(nMMIO_CS));
  PC pc_1 (
    .A_IN({int_vect_1_p3, int_vect_1_p3_2}), .PC_INC(PC_INC), .nPC_LD(nPC_LD), .PC_OE(PC_OE),
    .nPCL_OE(nPCL_OE), .nPCH_OE(nPCH_OE), .CLK(CLK_t), .RST(RST), .A_OUT({int_vect_1_p3, int_vect_1_p3_2}),
    .D_OUT(pc_1_d_out));
  SP sp_1 (
    .A_IN({int_vect_1_p3, int_vect_1_p3_2}), .nSP_INC(nSP_INC), .SP_DIR(SP_DIR), .nSP_LD(nSP_LD),
    .nSP_OE(nSP_OE), .nSPH_OE(nSPH_OE), .nSPL_OE(nSPL_OE), .CLK(CLK_t),
    .A_OUT({int_vect_1_p3, int_vect_1_p3_2}), .D_OUT(pc_1_d_out));
  MAR mar_1 (
    .D_IN(pc_1_d_out), .nMARL_LD(nMARL_LD), .nMARH_LD(nMARH_LD), .nMAR_OE(nMAR_OE), .nMAR_INC(nMAR_INC),
    .MAR_DIR(MAR_DIR), .CLK(CLK_t), .A_OUT({int_vect_1_p3, int_vect_1_p3_2}));
  RAMSinglePortSel #(.AddrBits(16), .Bits(8)) ramsingleportsel_1 (
    .A({int_vect_1_p3, int_vect_1_p3_2}), .CS(~addr_dec_1_nram_cs), .WE(MEM_WR), .OE(MEM_RD), .D(pc_1_d_out));
  EEPROM #(.AddrBits(15), .Bits(16)) eeprom_1 (
    .A({1'b0, int_vect_1_p3[5:0], int_vect_1_p3_2}), .CS(~addr_dec_1_nrom_cs), .WE(1'b0), .OE(MEM_RD), .D(rom));
  // IRQ_LATCH irq_latch_1: pin names not known; wires that end beside it: EXTERNAL_BUTTON, I, nCLR_IRQ, nMPC_RST, irq_latch_1_p5
  // RFILE rfile_1: pin names not known; wires that end beside it: pc_1_d_out, opcode[2:0], Rsrc, REG_LD, REG_OE, nXY_INC, XY_DIR, nXY_AOE, CLK_t, RST, pc_1_d_out, {int_vect_1_p3, int_vect_1_p3_2}, A_LD, A_OE
  ALU alu_1 (
    .D_IN(pc_1_d_out), .A_LD(A_LD), .A_OE(A_OE), .A_SEL(A_SEL), .ALU_S0(ALU_S0), .ALU_S1(ALU_S1),
    .ALU_S2(ALU_S2), .nALU_OE(nALU_OE), .ALU_CIN(ALU_CIN), .nSHR(nSHR), .SHR_IN0(SHR_IN0), .CLK(CLK_t),
    .RST(RST), .ALU(alu_1_alu), .Z_FLAG(alu_1_z_flag), .C_FLAG(alu_1_c_flag), .N_FLAG(alu_1_n_flag),
    .V_FLAG(alu_1_v_flag), .A_R_OUT(pc_1_d_out));
  // IR ir_1: pin names not known; wires that end beside it: rom, nIR_LD, nIRD_OE, nIRA_OE, CLK_t, opcode[7:3], opcode[2:0], Rsrc, pc_1_d_out, int_vect_1_p3_2
  microPC micropc_1 (.CLK(CLK_t), .nMPC_RST(nMPC_RST), .microstep(micropc_1_microstep));
  FLAG_REG flag_reg_1 (
    .D_IN(alu_1_alu), .Z_FLAG(alu_1_z_flag), .C_FLAG(alu_1_c_flag), .N_FLAG(alu_1_n_flag),
    .V_FLAG(alu_1_v_flag), .I_SET(I_SET), .I_WRITE(I_WRITE), .nFL_OE(B_SET), .nFL_LD(nFL_OE),
    .FL_SEL(nFL_LD), .FB(FL_SEL), .CLK(CLK_t), .nRST(nRST), .D_OUT(pc_1_d_out), .Z(Z), .C(C), .N(N), .V(V),
    .I(I));
  MMIO mmio_1 (
    .A_IN({int_vect_1_p3, int_vect_1_p3_2}), .D_IN(pc_1_d_out), .nMMIO_CS(nMMIO_CS), .CLK(CLK_t),
    .MEM_WR(MEM_WR), .MEM_RD(MEM_RD), .SPI_OUT(mmio_1_spi_out));
  CTRLUNIT ctrlunit_1 (
    .OPC(opcode), .microstep(micropc_1_microstep), .Z(Z), .C(C), .N(N), .V(V), .I(irq_latch_1_p5),
    .C0_15({nMAR_INC, nMAR_OE, nMARH_LD, nMARL_LD, MEM_WR, MEM_RD, nMPC_RST, nHBA_OE, nIRA_OE, nIRD_OE, nIR_LD, nPCH_OE, nPCL_OE, PC_OE, nPC_LD, PC_INC}),
    .C16_31({nFL_LD, nFL_OE, SHR_IN0, nSHR, ALU_CIN, nALU_OE, ALU_S2, ALU_S1, ALU_S0, A_SEL, nXY_AOE, XY_DIR, nXY_INC, REG_OE, REG_LD, MAR_DIR}),
    .C32_47({ctrlunit_1_c32_47, V_B0, nV_OE, nCLR_IRQ, nSPH_OE, nSPL_OE, nSP_OE, nSP_LD, SP_DIR, nSP_INC, I_WRITE, I_SET, B_SET, FL_SEL}));
  LED led_1 (.in(mmio_1_spi_out[0]));
  LED led_2 (.in(mmio_1_spi_out[1]));
  LED led_3 (.in(mmio_1_spi_out[2]));
  LED led_4 (.in(mmio_1_spi_out[3]));
  LED led_5 (.in(mmio_1_spi_out[4]));
  LED led_6 (.in(mmio_1_spi_out[5]));
  LED led_7 (.in(mmio_1_spi_out[6]));
  LED led_8 (.in(mmio_1_spi_out[7]));

  // Other names for the same wires on the sheet: Rdst[2:0] = opcode[2:0]

  // Notes on the sheet:
  //   clk_2: Hz: 10
  //   contents of eeprom_1 (hex, n*v repeats v):
  //   11bf,1000,ff,4000
endmodule
