// Digital circuit MMIO.dig as structural Verilog
module MMIO (
  input  [15:0] A_IN,
  input  [7:0] D_IN,
  input  nMMIO_CS,
  input  CLK,
  input  MEM_WR,
  input  MEM_RD,
  output [7:0] SPI_OUT
);

  wire _74138_1_pin15, MEM_WR_t;

  _74138 _74138_1 (
    .pin1(A_IN[0]), .pin2(A_IN[1]), .pin3(A_IN[2]), .pin4(nMMIO_CS), .pin5(1'b0), .pin6(1'b1), .pin8(1'b0),
    .pin15(_74138_1_pin15), .pin16(1'b1));  // open: pin7, pin9, pin10, pin11, pin12, pin13, pin14
  not not_1 (MEM_WR_t, MEM_WR);
  _74377 _74377_1 (
    .pin1(_74138_1_pin15), .pin2(SPI_OUT[0]), .pin3(D_IN[0]), .pin4(D_IN[1]), .pin5(SPI_OUT[1]),
    .pin6(SPI_OUT[2]), .pin7(D_IN[2]), .pin8(D_IN[3]), .pin9(SPI_OUT[3]), .pin10(1'b0), .pin11(MEM_WR_t),
    .pin12(SPI_OUT[4]), .pin13(D_IN[4]), .pin14(D_IN[5]), .pin15(SPI_OUT[5]), .pin16(SPI_OUT[6]),
    .pin17(D_IN[6]), .pin18(D_IN[7]), .pin19(SPI_OUT[7]), .pin20(1'b1));
endmodule
